# Fritzing sketch radar (saved by Fritzing 0.9.3b)
breadboards: 1

parts:
  Composant1 = Arduino Uno (Rev3)
  hc-sr1 = hc-sr04
  J1 = Basic Servo

nets:
  N1: Composant1.D8, hc-sr1.Trig
  N2: Composant1.D9_PWM, hc-sr1.Echo
  N3: Composant1.D12/MISO, J1.pulse
  VCC: Composant1.5V, hc-sr1.VCC, J1.vcc
  GND: Composant1.GND, hc-sr1.GND, J1.gnd
