# Fritzing sketch testIris (saved by Fritzing 0.9.3b)
breadboards: 1

parts:
  Composant1 = Arduino Uno (Rev3)
  Composant2 = Arduino Uno (Rev3)
  R1 = Resistor [tolerance=±5% resistance=1k package=THT]
  C1 = Electrolytic Capacitor [capacitance=4.7mF package="100 mil [THT, electrolytic]"]

nets:
  N1: Composant1.A4/SDA, Composant2.A4/SDA
  N2: Composant1.A5/SCL, Composant2.A5/SCL
  N3: Composant1.D12/MISO, Composant2.D12/MISO
  N4: Composant1.D13/SCK, Composant2.D13/SCK
  GND: Composant1.GND, Composant2.GND, C1.-
  N5: Composant2.A0, R1.Pin_0, C1.+
  N6: Composant2.D3_PWM, R1.Pin_1
